// Logisim project TARN.circ as structural Verilog: 2 circuits, main circuit main
module main (
);

  usage usage_1 ();  // open: A0, A1, A2, A3, A4, A5, A6, A7, IORQ, MREQ, RD_WR, ClockIn, D0, D1, D2, D3, D4, D5, D6, D7, OP0, OP1, OP2, OP3
endmodule

module usage (
  input  ClockIn,
  input  D0,
  input  D1,
  input  D2,
  input  D3,
  input  D4,
  input  D5,
  input  D6,
  input  D7,
  input  OP0,
  input  OP1,
  input  OP2,
  input  OP3,
  output A0,
  output A1,
  output A2,
  output A3,
  output A4,
  output A5,
  output A6,
  output A7,
  output IORQ,
  output MREQ,
  output RD_WR
);

  wire add, adder_1_cout, and_1_out, and_2_out, and_3_out, and_4_out, and_5_out, and_6_out, and_7_out,
       and_8_out, and_10_out, and_11_out, comparator_1_eq, comparator_2_eq, decoder_1_out0, decoder_1_out2,
       decoder_1_out3, decoder_1_out9, decoder_1_out10, decoder_1_out12, decoder_1_out13, decoder_1_out14,
       decoder_1_out15, eq, Jump_Enable_out, nan, nand_2_out, nor_3_out, not_1_out, not_2_out, notz,
       or_2_out, or_3_out, or_4_out, or_5_out, or_6_out, or_7_out, or_8_out, or_9_out, or_10_out, rr, sub,
       subtractor_1_bout, zero;
  wire [6:0] SP_q;
  wire [7:0] adder_1_out, and_9_out, controlled_buffer_1_out, controlled_buffer_7_out, nand_1_out, PC_q,
       shifter_1_out, subtractor_1_out, sum, xReg, yReg;
  wire [7:7] decoder_1_out1;

  or or_1 (eq, add, nan, sub, rr);
  Decoder #(.select(4)) decoder_1 (
    .out0(decoder_1_out0), .out1(decoder_1_out1[7]), .out2(decoder_1_out2), .out3(decoder_1_out3),
    .out4(add), .out5(sub), .out6(zero), .out7(notz), .out8(nan), .out9(decoder_1_out9),
    .out10(decoder_1_out10), .out11(rr), .out12(decoder_1_out12), .out13(decoder_1_out13),
    .out14(decoder_1_out14), .out15(decoder_1_out15), .sel({OP3, OP2, OP1, OP0}), .en(1'b1));
  assign controlled_buffer_1_out = or_2_out ? {D7, D6, D5, D4, D3, D2, D1, D0} : 8'bz;  // Controlled_Buffer controlled_buffer_1
  assign controlled_buffer_1_out = eq ? sum : 8'bz;  // Controlled_Buffer controlled_buffer_2
  Register X (.D(controlled_buffer_1_out), .en(and_1_out), .clk(and_1_out), .Q(xReg), .clr(1'b0));
  or or_2 (or_2_out, decoder_1_out3, decoder_1_out2);
  and and_1 (and_1_out, or_3_out, ClockIn);
  or or_3 (or_3_out, decoder_1_out2, eq);
  Adder adder_1 (.a(yReg), .b(xReg), .out(adder_1_out), .cin(1'b0), .cout(adder_1_cout));
  Subtractor subtractor_1 (.a(xReg), .b(yReg), .out(subtractor_1_out), .bin(1'b0), .bout(subtractor_1_bout));
  Comparator #(.mode("unsigned")) comparator_1 (.a(xReg), .b({8{1'b0}}), .eq(comparator_1_eq));  // open: gt, lt
  assign nand_1_out = ~(xReg & yReg);  // NAND_Gate nand_1, 8 bits wide
  Comparator #(.mode("unsigned")) comparator_2 (.a(xReg), .b({8{1'b0}}), .eq(comparator_2_eq));  // open: gt, lt
  assign sum = add ? adder_1_out : 8'bz;  // Controlled_Buffer controlled_buffer_3
  assign sum = sub ? subtractor_1_out : 8'bz;  // Controlled_Buffer controlled_buffer_4
  and and_2 (and_2_out, comparator_1_eq, zero);
  assign sum = nan ? nand_1_out : 8'bz;  // Controlled_Buffer controlled_buffer_5
  not not_1 (not_1_out, comparator_2_eq);
  assign sum = rr ? shifter_1_out : 8'bz;  // Controlled_Buffer controlled_buffer_6
  Shifter #(.shift("rr")) shifter_1 (.in(xReg), .\dist (yReg[2:0]), .out(shifter_1_out));
  not not_2 (not_2_out, ClockIn);
  or or_4 (or_4_out, decoder_1_out1[7], or_5_out);
  or or_5 (or_5_out, decoder_1_out14, decoder_1_out0);
  or Jump_Enable (Jump_Enable_out, decoder_1_out10, adder_1_cout, subtractor_1_bout, and_2_out, and_3_out);
  and and_3 (and_3_out, not_1_out, notz);
  and and_4 (and_4_out, not_2_out, or_4_out);
  and and_5 (and_5_out, or_5_out, ClockIn);
  or or_6 (or_6_out, or_7_out, or_9_out);
  or or_7 (or_7_out, and_5_out, and_6_out);
  and and_6 (and_6_out, decoder_1_out1[7], ClockIn);
  and and_7 (and_7_out, ClockIn, decoder_1_out12);
  or or_8 (or_8_out, or_5_out, decoder_1_out12);
  Counter #(.max('h7f), .width(7)) SP (
    .count(or_6_out), .Q(SP_q), .up(or_8_out), .clk(or_6_out));  // open: load, D, carry, clr
  or or_9 (or_9_out, and_7_out, and_8_out);
  and and_8 (and_8_out, ClockIn, decoder_1_out15);
  Counter PC (
    .load(Jump_Enable_out), .D({D7, D6, D5, D4, D3, D2, D1, D0}), .count(ClockIn), .Q(PC_q), .clk(ClockIn));  // open: carry, up, clr
  assign and_9_out = {D7, D6, D5, D4, D3, D2, D1, D0} & ~{8{decoder_1_out1[7]}};  // AND_Gate and_9, 8 bits wide
  RAM #(.addrWidth(7), .enables("line")) Stack (
    .addr(SP_q), .we(and_4_out), .clk(ClockIn), .din(and_9_out), .dout(yReg));
  nor nor_1 (IORQ, decoder_1_out13, decoder_1_out14);
  and and_10 (and_10_out, ~IORQ, ~ClockIn);  // AND_Gate
  or or_10 (or_10_out, and_10_out, decoder_1_out14, IORQ);
  assign controlled_buffer_7_out = or_10_out ? PC_q : 8'bz;  // Controlled_Buffer controlled_buffer_7
  nor nor_2 (MREQ, decoder_1_out3, decoder_1_out9);
  nor nor_3 (nor_3_out, ~decoder_1_out3, decoder_1_out9);  // NOR_Gate
  nand nand_2 (nand_2_out, decoder_1_out3, decoder_1_out9);
  nand nand_3 (RD_WR, nor_3_out, nand_2_out);
  and and_11 (and_11_out, ClockIn, decoder_1_out13);
  assign {A7, A6, A5, A4, A3, A2, A1, A0} = and_11_out ? yReg : 8'bz;  // Controlled_Buffer controlled_buffer_8
  assign {A7, A6, A5, A4, A3, A2, A1, A0} = controlled_buffer_7_out;  // Buffer buffer_1, 8 bits wide

  // Other names for the same wires on the sheet: Data[7:0] = {D7, D6, D5, D4, D3, D2, D1, D0}
endmodule
